# Fritzing sketch Blink (saved by Fritzing 0.9.3b)
breadboards: 1

parts:
  Part1 = Arduino Uno (Rev3) - ICSP
  R1 = Resistor [tolerance=±5% resistance=220 package=THT]
  LED1 = LEDs [package=led10mm]

nets:
  N1: Part1.GND, LED1.C
  N2: Part1.D9_PWM, R1.Pin_0
  N3: R1.Pin_1, LED1.A
